# Fritzing sketch 2022-TC-Grupo4-Lab3-Fritzing-Circuit (saved by Fritzing 0.9.3b)
breadboards: 1

parts:
  Mod1 = Raspberry Pi Pico
  Componente1 = XBee Explorer Regulated
  M1 = DC Motor
  Q1 = LTR-301 [package=ltr-301]
  J1 = Piezo Speaker

nets:
  N1: Mod1.pin_5, Q1.E
  N2: Mod1.pin_8, Mod1.pin_18, Mod1.pin_23, Mod1.pin_33, Mod1.pin_42, Componente1.GND, Q1.C, J1.pin1
  N3: Mod1.pin_17, Componente1.DIN, Componente1.5V
  N4: Mod1.pin_22, J1.pin2
  N5: Componente1.DOUT, M1.pin_2

custom parts:
  Raspberry Pi Pico: Raspberry Pi Pico. Based around the RP2040 microcontroller the Pico is a low cost microcontroller device bringing Raspberry Pi quality, cost, and easy of use to the microcontroller space. Jan 2021, Split part in to two versions: tht (this one) and SMD. This one will drill holes for a .1 in header in pcb to allow plugging in the module as well as providing pads to solder the module to the top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
