# Fritzing sketch master-slave ard rasp (saved by Fritzing 0.9.3b)
breadboards: 1

parts:
  Mod1 = Raspberry Pi Pico W
  Part1 = Arduino Uno (Rev3) - ICSP
  S1 = Tilt Switch [package=THT]
  M1 = DC Motor
  J1 = Piezo Speaker
  K1 = Relay [part_number=FRS1B-S package=THT]  # not connected

nets:
  N1: Mod1.pin_1, Part1.A4/SDA
  N2: Mod1.pin_2, Part1.A5/SCL
  N3: Mod1.pin_3, Mod1.pin_8, Mod1.pin_13, Mod1.pin_18, Mod1.pin_23, Mod1.pin_28, Mod1.pin_33, Mod1.pin_38, Mod1.pin_42, Part1.GND, S1.Pin_1, M1.pin_1, J1.pin1
  N4: Mod1.pin_17, J1.pin2
  N5: Mod1.pin_21, S1.Pin_2
  N6: Mod1.pin_40, Part1.VIN

custom parts:
  Raspberry Pi Pico W: Raspberry Pi Pico W. Based around the RP2040 microcontroller the Pico W is a low cost microcontroller device bringing Raspberry Pi quality, cost, and easy of use to the microcontroller space. The areas marked KEEPOUT in pcb silkscreen should not have traces running through them to avoid shorts on a soldered in module!
